# Fritzing sketch Balancing Robot (saved by Fritzing 0.9.3b)

parts:
  GY1 = MPU-6050 Board GY-521 [form="♀ (female)" package=THT]
  U1 = ESP8266 WiFi Module [part_number=ESP8266]
  VCC1 = Battery
  S1 = Taiway 100-SP-X-T1 SPDT Miniature Toggle Switch [part_number=100-SP-X-T1-0-0-B1-M1 package=THT]
  U2 = Mini-360 DC-DC Buck converter [package=THT]
  C1 = Electrolytic Capacitor [capacitance=500µF package="100 mil [THT, electrolytic]"]
  R1 = Trimmer Potentiometer [maximum_resistance=100kΩ package=THT]
  M1 = DC Motor
  M2 = DC Motor
  U3 = L298_BRIDGE_DRIVER [package=powerso20]
  R2 = Resistor [tolerance=±5% resistance=100k package=THT]
  R3 = Resistor [tolerance=±5% resistance=100k package=THT]

nets:
  N1: GY1.pin1, U1.VCC, U1.CH_PD, U2.OUT+, C1.+, R2.Pin_0, R3.Pin_0
  N2: GY1.pin2, U1.GND, U2.OUT-, C1.-
  N3: GY1.pin3, U1.TXD
  N4: GY1.pin4, U1.RXD
  N5: U1.GPIO_0, U3.IN2
  N6: U1.GPIO_2, U3.IN1
  N7: VCC1.-, U2.IN-, R1.leg2, U3.GND
  N8: VCC1.+, S1.L2
  N9: S1.COM, U2.IN+, R1.leg1, U3.VS
  N10: M1.pin_1, U3.OUT4
  N11: M1.pin_2, U3.OUT3
  N12: M2.pin_1, U3.OUT2
  N13: M2.pin_2, U3.OUT1
  N14: U3.IN3, U3.IN4

notes:
  Solder yellow pins directly to the chip.
  From the trim pot -> TOUT (pin 6 - ADC)
  From IN1/IN2 -> MTMS/MTDI (pins 9/10)
  Before powering MPU and ESP:
  Adjust 100k trim to 1/10th of max cell voltage
  Adjust dc-dc regulator to 3.3V
  Batteries: 18650 LiIon cells
  Geared motors of your liking

custom parts:
  MPU-6050 Board GY-521: Acelerometro y Giroscopio MPU-6050 Board GY-521
  ESP8266 WiFi Module: Generic WiFi Module based on the ESP8266 with onboard PCB antenna and UART communications
  Mini-360 DC-DC Buck converter: Mini-360 DC-DC Buck converter. Tiny buck step down voltage converter, input voltage 4.75 to 23V output 1 to 17V adjustable. Available from ebay and the like.
